# Fritzing sketch schema (saved by Fritzing 0.9.4)
breadboards: 1

parts:
  U1 = ESP8266 NodeMCU LoLin module
  DHT1 = DHT11 Humitidy and Temperature Sensor
  R1 = Resistor [tolerance=±5% resistance=10k package=THT]

nets:
  N1: U1.D2, DHT1.DATA, R1.Pin_1
  3V3: U1.3V3, DHT1.VDD, R1.Pin_0
  GND: U1.GND, DHT1.GND

custom parts:
  ESP8266 NodeMCU LoLin module: ESP8266 based NodeMCU
  DHT11 Humitidy and Temperature Sensor: DHT11 Humidity and Temperature Sensor
